# Fritzing sketch ESP32-WROVER-windchimes (saved by Fritzing 0.9.6b)

parts:
  M1 = Dagu DGServo 9g (Top view) [part_number=RS001B]
  M2 = Dagu DGServo 9g (Top view) [part_number=RS001B]
  Part1 = Adafruit MAX98357A I2S 3W Class D Amplifier [part_number="Adafruit #3006"]
  U1 = ESP32-40-pin [part_number=ESP32S-HiLetgo]
  C1 = Electrolytic Capacitor [capacitance=0.47mF voltage=35V package="0807 [SMD, electrolytic]"]
  M3 = Dagu DGServo 9g (Top view) [part_number=RS001B]
  SPKR1 = Loudspeaker  # not connected

nets:
  GND: M1.gnd, M2.gnd, Part1.GND, U1.GND, C1.-, M3.gnd
  VCC: M1.vcc, M2.vcc, Part1.VIN, U1.VIN, C1.+, M3.vcc
  N1: M1.pulse, U1.GPIO14
  N2: M2.pulse, U1.GPIO13
  N3: Part1.DIN, U1.GPIO22
  N4: Part1.BCLK, U1.GPIO26
  N5: Part1.LRCLK, U1.GPIO25
  N6: U1.GPIO33, M3.pulse

custom parts:
  Adafruit MAX98357A I2S 3W Class D Amplifier: Listen to this good news - we now have an all in one digital audio amp breakout board that works incredibly well with the Raspberry Pi! If you're looking for an easy and low cost way to get you digital sound files bumpin' then the MAX08357 I2S Amp Breakout is for you. It takes standard I2S digital audio input and, not only decodes it into analog, but also amplifies it directly into a speaker.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
  ESP32-40-pin: HiLetgo ESP-WROOM-32 ESP32 ESP-32S Development Board 2.4GHz Dual-Mode WiFi + Bluetooth Dual Cores Microcontroller The ESP32 integrated with Antenna switches, RF Balun, power amplifiers, low-noise amplifiers, filters, and management modules, and the entire solution occupies the least area of PCB. 2.4 GHz Wi-Fi plus Bluetooth dual-mode chip, with TSMC Ultra-low power consumption 40nm technology,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
